# Fritzing sketch Farm Project (saved by Fritzing 1.0.4)
breadboards: 1

parts:
  module1 = MQ-2 Gas Sensor
  CPU1 = NodeMCU WROOM ESP 32
  R1 = Resistor [tolerance=±5% power=0.25W resistance=10k package=THT]
  R2 = Resistor [tolerance=±5% power=0.25W resistance=10k package=THT]

nets:
  N1: module1.AO, R1.Pin_1
  N2: module1.VCC, CPU1.pin_16
  N3: module1.GND, CPU1.pin_15, R2.Pin_0
  N4: CPU1.pin_5, R1.Pin_0, R2.Pin_1

custom parts:
  MQ-2 Gas Sensor: MQ-2 Gas Sensor module of SunFounder Sensor Kit
  NodeMCU WROOM ESP 32: 30 pol Development Kit
